# Fritzing sketch palačinka (saved by Fritzing 0.9.2b)
circuit board: 8.46667cm x 5.64444cm
breadboards: 1

parts:
  Q5 = NPN-Transistor [package="TO92 [THT]"]
  R6 = Temperature Sensor (Thermistor) [thermistor_type=NTC package=THT]
  M1 = DC Motor
  Power_plug1 = Power plug
  R8 = Temperature Sensor (Thermistor) [thermistor_type=NTC package=THT]
  Q1 = NPN-Transistor [package="TO92 [THT]"]
  Q4 = NPN-Transistor [package="TO92 [THT]"]
  R7 = Resistor [tolerance=±5% resistance=220 package=THT]
  M2 = DC Motor
  L1 = Solenoid
  Q2 = NPN-Transistor [package="TO92 [THT]"]
  R1 = Resistor [tolerance=±5% resistance=220 package=THT]
  R2 = Resistor [tolerance=±5% resistance=1M package=THT]
  R4 = Temperature Sensor (Thermistor) [thermistor_type=NTC package=THT]
  J1 = Infrared Proximity Sensor
  Part1 = Arduino Mega 2560 (Rev3)
  Q3 = NPN-Transistor [package="TO92 [THT]"]
  R9 = Resistor [tolerance=±5% resistance=220 package=THT]
  R3 = Resistor [tolerance=±5% resistance=1M package=THT]
  R5 = Resistor [tolerance=±5% resistance=220 package=THT]

nets:
  N1: Q5.E, Power_plug1.GND, Q1.E, Q2.E, R1.Pin_1
  N2: Q5.B, Part1.D30
  N3: Q5.C, L1.pin1
  N4: R6.pin_0, R7.Pin_1, Part1.A1
  VCC: R6.pin_1, R8.pin_1, R4.pin_1, J1.Vcc, Part1.5V
  N5: M1.pin_1, Power_plug1.VCC, Q4.E, M2.pin_1, L1.pin2, R2.Pin_0, Q3.E, R3.Pin_0
  N6: M1.pin_2, Q1.C
  N7: R8.pin_0, Part1.A2, R9.Pin_1
  N8: Q1.B, Part1.D2_PWM
  N9: Q4.B, Part1.D28
  N10: Q4.C, R3.Pin_1
  GND: R7.Pin_0, R1.Pin_0, J1.GND, Part1.GND, R9.Pin_0, R5.Pin_0
  N11: M2.pin_2, Q2.C
  N12: Q2.B, Part1.D3_PWM
  N13: R2.Pin_1, Q3.C
  N14: R4.pin_0, Part1.A0, R5.Pin_1
  N15: J1.Vout, Part1.D23
  N16: Part1.D26, Q3.B

notes:
  Ventil
  Grelca
  Zunanje napajanje
  Ultrazvok za nivo mase
  Trak
  Mikser
  Terimstorji za maso

// code stored in the sketch: palaΦinka.ino


// code stored in the sketch: pala?inka.ino

